# Fritzing sketch SmartPlantSystem (saved by Fritzing 0.9.9b)
breadboards: 1

parts:
  OLED_I2C1 = OLED 128x64 I2C Monochrome Display
  Argon1 = Particle Argon
  SENS1 = SoilWatch 10
  M1 = BMP280
  Part1 = 12 NeoPixel Ring [part_number=1643]
  Part2 = MQ-131 breakout
  Grove1 = Grove Dust Sensor
  WATER_PUMP1 = water pump/motor  # not connected
  Relay1 = Relay - 6 pins [package="DIP (Dual Inline) [THT]"]
  R1 = Resistor [tolerance=±5% resistance=2.2k package="2010 [SMD]"]
  Q1 = PNP-Transistor [package="TO92 [THT]"]
  R2 = Resistor [tolerance=±5% resistance=47 package="2010 [SMD]"]

nets:
  N1: OLED_I2C1.SDA, Argon1.SDA, M1.SDA
  N2: OLED_I2C1.SCK, Argon1.SCL, M1.SCL
  VDD: OLED_I2C1.VDD, M1.VIN, Part1.VDD, Relay1.ON, R2.Pin_0
  GND: OLED_I2C1.GND, Argon1.GND, SENS1.GND, M1.GND, Part1.GND, Part2.GND, Grove1.GND, Relay1.GND, R1.Pin_0, Q1.C
  VCC: Argon1.3.3V, SENS1.VCC, Part2.VCC, Grove1.VCC, Relay1.VCC
  N3: Argon1.A0, SENS1.OUT
  N4: Argon1.A1, Part2.DO
  N5: Argon1.A2, Grove1.SIG
  N6: Argon1.MI, Relay1.IN, R1.Pin_1, Q1.B
  N7: Argon1.D2, Part1.IN
  N8: Q1.E, R2.Pin_1

custom parts:
  Particle Argon: The Argon is a powerful Wi-Fi enabled development board that can act as either a standalone Wi-Fi endpoint or Wi-Fi enabled gateway for Particle Mesh networks. It is based on the Nordic nRF52840 and has built-in battery charging circuitry so it’s easy to connect a Li-Po and deploy your local network in minutes. The Argon is great for connecting existing projects to the Particle Device Cloud or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
  SoilWatch 10: SoilWatch 10 - Capacitive soil moisture sensor
  BMP280: Temperature Humidity Barometric presure Sensor, I2C
  12 NeoPixel Ring: 12 ultra bright smart LED NeoPixels are arranged in a circle with 1.5" (37mm) outer diameter. The rings are 'chainable' - connect the output pin of one to the input pin of another. Use only one microcontroller pin to control as many as you can chain together! Each LED is addressable as the driver chip is inside the LED. Each one has ~18mA constant current drive so the color will be very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
  MQ-131 breakout: SKU: 101282
  Grove Dust Sensor: PPD42 Grove Dust Sensor
  water pump/motor: WATER PUMP BY ARDUBLOCKTR
  Relay - 6 pins: A DIP stand-in part for whatever IC you want. With 6 pins on a 900mil dual inline package (DIP) footprint.
